// Logisim project bcd_adder.circ as structural Verilog: 4 circuits, main circuit main
module main (
  input  [3:0] A100,
  input  [3:0] B100,
  input  [3:0] A10,
  input  [3:0] B10,
  input  [3:0] A1,
  input  [3:0] B1,
  input  Cin,
  output [3:0] S100,
  output Cout,
  output [3:0] S10,
  output [3:0] S1
);

  wire Cout1, Cout10;

  bcd_digit digit_100 (.Cin(Cout10), .A(A100), .B(B100), .Cout(Cout), .S(S100));
  bcd_digit digit_10 (.Cin(Cout1), .A(A10), .B(B10), .Cout(Cout10), .S(S10));
  bcd_digit digit_1 (.Cin(Cin), .A(A1), .B(B1), .Cout(Cout1), .S(S1));
  Hex_Digit_Display hex_digit_display_1 (.value(S100));  // open: dp
  LED led_1 (.in(Cout));
  Hex_Digit_Display hex_digit_display_2 (.value(S10));  // open: dp
  Hex_Digit_Display hex_digit_display_3 (.value(S1));  // open: dp
endmodule

module full_adder (
  input  A,
  input  B,
  input  Cin,
  output Sum,
  output Cout
);

  wire P1, P2, X1;

  xor xor_1 (X1, A, B);
  and and_1 (P1, A, B);
  xor xor_2 (Sum, X1, Cin);
  and and_2 (P2, X1, Cin);
  or or_1 (Cout, P1, P2);
endmodule

module adder4 (
  input  Cin,
  input  [3:0] A,
  input  [3:0] B,
  output [3:0] Sum,
  output Cout
);

  wire CY0, CY1, CY2;

  full_adder FA3 (.A(A[3]), .B(B[3]), .Cin(CY2), .Sum(Sum[3]), .Cout(Cout));
  full_adder FA2 (.A(A[2]), .B(B[2]), .Cin(CY1), .Sum(Sum[2]), .Cout(CY2));
  full_adder FA1 (.A(A[1]), .B(B[1]), .Cin(CY0), .Sum(Sum[1]), .Cout(CY1));
  full_adder FA0 (.A(A[0]), .B(B[0]), .Cin(Cin), .Sum(Sum[0]), .Cout(CY0));

  // Other names for the same wires on the sheet: CoutH = Cout; S0 = Sum[0]; S1 = Sum[1]; S2 = Sum[2]; S3 = Sum[3]
endmodule

module bcd_digit (
  input  Cin,
  input  [3:0] A,
  input  [3:0] B,
  output [3:0] S,
  output Cout
);

  wire C1, GT;
  wire [3:0] and_1_out, bit_extender_1_out, Z;

  adder4 adder4_1 (.A(A), .B(B), .Cin(Cin), .Sum(Z), .Cout(C1));
  assign bit_extender_1_out = {{3{Cout}}, Cout};  // Bit_Extender bit_extender_1
  or or_1 (Cout, C1, GT);
  assign and_1_out = 4'b0110 & bit_extender_1_out;  // AND_Gate and_1, 4 bits wide
  Comparator #(.mode("unsigned"), .width(4)) comparator_1 (.a(Z), .b(4'b1001), .gt(GT));  // open: eq, lt
  adder4 adder4_2 (.A(Z), .B(and_1_out), .Cin(1'b0), .Sum(S));  // open: Cout
  Hex_Digit_Display hex_digit_display_1 (.value(S));  // open: dp

  // Other names for the same wires on the sheet: CORR = Cout
endmodule
